# Fritzing sketch arduinoSketch (saved by Fritzing 0.9.3b)
breadboards: 1

parts:
  부품1 = Arduino Uno (Rev3)
  VCC1 = Battery
  Adafruit_HUZZAH_ESP8266_Breakout1 = Adafruit HUZZAH ESP8266 Breakout [part_number=2471]
  J1 = Basic Servo
  J2 = Basic Servo
  J3 = Basic Servo

nets:
  N1: 부품1.D9_PWM, J3.pulse
  N2: 부품1.D10_PWM/SS, J1.pulse
  N3: 부품1.D11_PWM/MOSI, J2.pulse
  N4: 부품1.D2, Adafruit_HUZZAH_ESP8266_Breakout1.TX
  N5: 부품1.D3_PWM, Adafruit_HUZZAH_ESP8266_Breakout1.RX
  N6: 부품1.5V, Adafruit_HUZZAH_ESP8266_Breakout1.V+
  GND: 부품1.GND, VCC1.-, Adafruit_HUZZAH_ESP8266_Breakout1.GND, J1.gnd, J2.gnd, J3.gnd
  VCC: VCC1.+, J1.vcc, J2.vcc
